// Logisim project 2_input_mux.circ as structural Verilog: 1 circuit, main circuit main
module main (
  input  In0,
  input  In1,
  input  s,
  output out_4
);

  wire and_1_out, and_2_out, not_1_out;

  and and_1 (and_1_out, In0, not_1_out);
  not not_1 (not_1_out, s);
  and and_2 (and_2_out, In1, s);
  or or_1 (out_4, and_1_out, and_2_out);
endmodule
