// Logisim project 4_input_mux.circ as structural Verilog: 1 circuit, main circuit main
module main (
  input  In0,
  input  In1,
  input  In2,
  input  In3,
  input  s0,
  input  s1,
  output out_7
);

  wire and_1_out, and_2_out, and_3_out, and_4_out, and_5_out, and_6_out, and_7_out, and_8_out, not_1_out,
       not_2_out, not_3_out, not_4_out, or_1_out, or_2_out;

  not not_1 (not_1_out, s0);
  not not_2 (not_2_out, s0);
  and and_1 (and_1_out, In0, not_1_out);
  and and_2 (and_2_out, In1, s0);
  and and_3 (and_3_out, In2, not_2_out);
  and and_4 (and_4_out, In3, s0);
  and and_5 (and_5_out, and_1_out, not_3_out);
  not not_3 (not_3_out, s1);
  and and_6 (and_6_out, and_2_out, not_4_out);
  not not_4 (not_4_out, s1);
  and and_7 (and_7_out, and_3_out, s1);
  and and_8 (and_8_out, and_4_out, s1);
  or or_1 (or_1_out, and_5_out, and_6_out);
  or or_2 (or_2_out, and_7_out, and_8_out);
  or or_3 (out_7, or_1_out, or_2_out);
endmodule
