// Logisim project Adder.circ as structural Verilog: 1 circuit, main circuit main
module main (
  input  carry_in,
  input  a0,
  input  b0,
  input  a1,
  input  b1,
  input  a2,
  input  b2,
  input  a3,
  input  b3,
  output Output,
  output Output_2,
  output Output_3,
  output Output_4
);

  wire and_1_out, and_2_out, and_3_out, and_4_out, and_5_out, and_6_out, and_7_out, and_8_out, and_9_out,
       and_10_out, and_11_out, and_12_out, and_13_out, and_14_out, and_15_out, and_16_out, and_17_out,
       and_18_out, and_19_out, and_20_out, and_21_out, and_22_out, and_23_out, and_24_out, and_25_out,
       and_26_out, and_27_out, and_28_out, and_29_out, and_30_out, and_31_out, and_32_out, not_1_out,
       not_2_out, not_3_out, not_4_out, not_5_out, not_6_out, not_7_out, not_8_out, not_9_out, not_10_out,
       not_11_out, not_12_out, not_13_out, not_14_out, not_15_out, not_16_out, not_17_out, not_18_out,
       not_19_out, not_20_out, not_21_out, not_22_out, not_23_out, not_24_out, not_25_out, not_26_out,
       not_27_out, not_28_out, not_29_out, not_30_out, not_31_out, not_32_out, not_33_out, not_34_out,
       not_35_out, not_36_out, or_2_out, or_4_out, or_6_out;

  not not_1 (not_1_out, a0);
  and and_1 (and_1_out, not_1_out, b0, not_2_out);
  not not_2 (not_2_out, carry_in);
  not not_3 (not_3_out, a0);
  and and_2 (and_2_out, not_3_out, not_4_out, carry_in);
  not not_4 (not_4_out, b0);
  and and_3 (and_3_out, a0, not_5_out, not_6_out);
  not not_5 (not_5_out, b0);
  not not_6 (not_6_out, carry_in);
  and and_4 (and_4_out, a0, b0, carry_in);
  not not_7 (not_7_out, a0);
  and and_5 (and_5_out, not_7_out, b0, carry_in);
  not not_8 (not_8_out, b0);
  and and_6 (and_6_out, a0, not_8_out, carry_in);
  and and_7 (and_7_out, a0, b0, not_9_out);
  not not_9 (not_9_out, carry_in);
  and and_8 (and_8_out, a0, b0, carry_in);
  not not_10 (not_10_out, a1);
  not not_11 (not_11_out, or_2_out);
  not not_12 (not_12_out, a1);
  not not_13 (not_13_out, b1);
  not not_14 (not_14_out, b1);
  not not_15 (not_15_out, or_2_out);
  not not_16 (not_16_out, a1);
  not not_17 (not_17_out, b1);
  not not_18 (not_18_out, or_2_out);
  not not_19 (not_19_out, a2);
  not not_20 (not_20_out, or_4_out);
  not not_21 (not_21_out, a2);
  not not_22 (not_22_out, b2);
  not not_23 (not_23_out, b2);
  not not_24 (not_24_out, or_4_out);
  not not_25 (not_25_out, a2);
  not not_26 (not_26_out, b2);
  not not_27 (not_27_out, or_4_out);
  and and_9 (and_9_out, not_10_out, b1, not_11_out);
  and and_10 (and_10_out, not_12_out, not_13_out, or_2_out);
  and and_11 (and_11_out, a1, not_14_out, not_15_out);
  and and_12 (and_12_out, a1, b1, or_2_out);
  and and_13 (and_13_out, not_16_out, b1, or_2_out);
  and and_14 (and_14_out, a1, not_17_out, or_2_out);
  and and_15 (and_15_out, a1, b1, not_18_out);
  and and_16 (and_16_out, a1, b1, or_2_out);
  and and_17 (and_17_out, not_19_out, b2, not_20_out);
  and and_18 (and_18_out, not_21_out, not_22_out, or_4_out);
  and and_19 (and_19_out, a2, not_23_out, not_24_out);
  and and_20 (and_20_out, a2, b2, or_4_out);
  and and_21 (and_21_out, not_25_out, b2, or_4_out);
  and and_22 (and_22_out, a2, not_26_out, or_4_out);
  and and_23 (and_23_out, a2, b2, not_27_out);
  and and_24 (and_24_out, a2, b2, or_4_out);
  not not_28 (not_28_out, a3);
  not not_29 (not_29_out, or_6_out);
  not not_30 (not_30_out, a3);
  not not_31 (not_31_out, b3);
  not not_32 (not_32_out, b3);
  not not_33 (not_33_out, or_6_out);
  not not_34 (not_34_out, a3);
  not not_35 (not_35_out, b3);
  not not_36 (not_36_out, or_6_out);
  and and_25 (and_25_out, not_28_out, b3, not_29_out);
  and and_26 (and_26_out, not_30_out, not_31_out, or_6_out);
  and and_27 (and_27_out, a3, not_32_out, not_33_out);
  and and_28 (and_28_out, a3, b3, or_6_out);
  and and_29 (and_29_out, not_34_out, b3, or_6_out);
  and and_30 (and_30_out, a3, not_35_out, or_6_out);
  and and_31 (and_31_out, a3, b3, not_36_out);
  and and_32 (and_32_out, a3, b3, or_6_out);
  or or_1 (Output, and_1_out, and_2_out, and_3_out, and_4_out);
  or or_2 (or_2_out, and_5_out, and_6_out, and_7_out, and_8_out);
  or or_3 (Output_2, and_9_out, and_10_out, and_11_out, and_12_out);
  or or_4 (or_4_out, and_13_out, and_14_out, and_15_out, and_16_out);
  or or_5 (Output_3, and_17_out, and_18_out, and_19_out, and_20_out);
  or or_6 (or_6_out, and_21_out, and_22_out, and_23_out, and_24_out);
  or or_7 (Output_4, and_25_out, and_26_out, and_27_out, and_28_out);
  // OR_Gate or_8 has open pins: in0=and_29_out, in1=and_30_out, in2=and_31_out, in3=and_32_out, out=open
endmodule
