// Logisim project alu.circ as structural Verilog: 1 circuit, main circuit main
module main (
  input  carry_in,
  input  a0,
  input  b0,
  input  a1,
  input  b1,
  input  a2,
  input  b2,
  input  a3,
  input  b3,
  input  in_10,
  input  in_11,
  output out_12,
  output out_13,
  output out_14,
  output out_15
);

  wire and_1_out, and_2_out, and_3_out, and_4_out, main_1_output, main_1_output_2, main_1_output_3,
       main_1_output_4, main_2_output, main_2_output_2, main_2_output_3, main_2_output_4, not_1_out,
       not_2_out, not_3_out, not_4_out, or_1_out, or_2_out, or_3_out, or_4_out;

  not not_1 (not_1_out, b0);
  not not_2 (not_2_out, b1);
  not not_3 (not_3_out, b2);
  not not_4 (not_4_out, b3);
  and and_1 (and_1_out, a0, b0);
  or or_1 (or_1_out, a0, b0);
  and and_2 (and_2_out, a1, b1);
  or or_2 (or_2_out, a1, b1);
  and and_3 (and_3_out, a2, b2);
  or or_3 (or_3_out, a2, b2);
  and and_4 (and_4_out, a3, b3);
  or or_4 (or_4_out, a3, b3);
  Adder_main main_1 (
    .carry_in(carry_in), .a0(a0), .b0(b0), .a1(a1), .b1(b1), .a2(a2), .b2(b2), .a3(a3), .b3(b3),
    .Output(main_1_output), .Output_2(main_1_output_2), .Output_3(main_1_output_3), .Output_4(main_1_output_4));
  Adder_main main_2 (
    .carry_in(carry_in), .a0(a0), .b0(not_1_out), .a1(a1), .b1(not_2_out), .a2(a2), .b2(not_3_out), .a3(a3),
    .b3(not_4_out), .Output(main_2_output), .Output_2(main_2_output_2), .Output_3(main_2_output_3),
    .Output_4(main_2_output_4));
  _4_input_mux_main main_3 (
    .In0(and_1_out), .In1(or_1_out), .In2(main_1_output), .In3(main_2_output), .s0(in_10), .s1(in_11),
    .out_7(out_12));
  _4_input_mux_main main_4 (
    .In0(and_2_out), .In1(or_2_out), .In2(main_1_output_2), .In3(main_2_output_2), .s0(in_10), .s1(in_11),
    .out_7(out_13));
  _4_input_mux_main main_5 (
    .In0(and_3_out), .In1(or_3_out), .In2(main_1_output_3), .In3(main_2_output_3), .s0(in_10), .s1(in_11),
    .out_7(out_14));
  _4_input_mux_main main_6 (
    .In0(and_4_out), .In1(or_4_out), .In2(main_1_output_4), .In3(main_2_output_4), .s0(in_10), .s1(in_11),
    .out_7(out_15));
endmodule
