// Logisim project circuit.circ as structural Verilog: 1 circuit, main circuit main
module main (
  input  clock,
  input  write_enable,
  input  carry_in,
  input  write_enable_2,
  input  write_enable_3,
  input  in_6,
  input  in_7,
  input  in_8,
  input  in_9,
  input  in_10,
  input  in_11,
  input  in_12,
  input  in_13,
  input  s,
  input  in_15,
  output out_16,
  output out_17,
  output out_18,
  output out_19
);

  wire main_1_out_8, main_1_out_9, main_1_out_10, main_1_q, main_2_out_8, main_2_out_9, main_2_out_10,
       main_2_q, main_3_out_12, main_3_out_13, main_3_out_14, main_3_out_15;

  _4_bit_register_main main_1 (
    .write_enable(write_enable_3), .clock(clock), .data_0(in_6), .data_1(in_7), .data_2(in_8), .data_3(in_9),
    .Q(main_1_q), .out_8(main_1_out_8), .out_9(main_1_out_9), .out_10(main_1_out_10));
  _4_bit_register_main main_2 (
    .write_enable(write_enable), .clock(clock), .data_0(in_10), .data_1(in_11), .data_2(in_12),
    .data_3(in_15), .Q(main_2_q), .out_8(main_2_out_8), .out_9(main_2_out_9), .out_10(main_2_out_10));
  alu_main main_3 (
    .carry_in(carry_in), .a0(main_1_q), .b0(main_1_out_8), .a1(main_1_out_9), .b1(main_1_out_10),
    .a2(main_2_q), .b2(main_2_out_8), .a3(main_2_out_9), .b3(main_2_out_10), .in_10(in_13), .in_11(s),
    .out_12(main_3_out_12), .out_13(main_3_out_13), .out_14(main_3_out_14), .out_15(main_3_out_15));
  _4_bit_register_main main_4 (
    .write_enable(write_enable_2), .clock(clock), .data_0(main_3_out_12), .data_1(main_3_out_13),
    .data_2(main_3_out_14), .data_3(main_3_out_15), .Q(out_16), .out_8(out_17), .out_9(out_18),
    .out_10(out_19));

  // Notes on the sheet:
  //   s
endmodule
